# Fritzing sketch Thermostat (saved by Fritzing 0.8.7b)

parts:
  Part1 = OLED Monochrome 128x64 0.96 inch [part_number=326]
  Raspberry_Pi1 = Raspberry Pi Zero
  DHT1 = DHT22 Humidity and Temperature Sensor
  R2 = Resistor [tolerance=±5% resistance=10k package=THT]  # not connected
  S1 = Pushbutton [package="[THT]"]
  S2 = Pushbutton [package="[THT]"]
  Part2 = Adafruit PowerRelay Feather Wing [part_number="Adafruit #3191"]

nets:
  N1: Part1.MOSI_SDA, Raspberry_Pi1.GPIO2
  N2: Part1.SCLK_SCK, Raspberry_Pi1.GPIO3
  N3: Part1.RESET, Raspberry_Pi1.GIPO4
  3V3: Part1.VIN, Raspberry_Pi1.3v3, Raspberry_Pi1.3V3, S1.Pin_3, S1.Pin_4
  N4: Part1.GND, Raspberry_Pi1.GIPO18
  GND: Raspberry_Pi1.GND, DHT1.GND, Part2.GND
  N5: Raspberry_Pi1.GIPO17, Part2.RELAY
  N6: Raspberry_Pi1.GIPO27, S2.Pin_1
  N7: Raspberry_Pi1.GIPO22, DHT1.DATA
  N8: Raspberry_Pi1.GIPO23, S1.Pin_1, S1.Pin_2
  5V: Raspberry_Pi1.5V, DHT1.VDD, Part2.RESET

notes:
  REMOVE R1 FROM RELAY

custom parts:
  OLED Monochrome 128x64 0.96 inch: These displays are small, only about 1" diameter, but very readable due to the high contrast of an OLED display. This display is made of 128x64 individual white OLED pixels, each one is turned on or off by the controller chip. Because the display makes its own light, no backlight is required. This reduces the power required to run the OLED and is why the display has such high contrast; we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
  Raspberry Pi Zero: The Raspberry Pi Zero is the latest single board computer to be released by the Raspberry Pi Foundation. It is the entry level model Raspberry Pi perfect for hobbyists, makers and industrial engineers looking to create solutions where small size and low power consumption are important. This is especially relevant for applications in the wearables space as well as up and coming applications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
  Adafruit PowerRelay Feather Wing: A Feather board without ambition is a Feather board without FeatherWings! This is the Power Relay FeatherWing. It gives you power to control, and control over power. Put simply, you can now turn on and off lamps, fans, solenoids, and other small appliances that run on up to 250VAC or DC power using any Feather board. Compared to our smaller Relay FeatherWings, this one can handle a beefy 1200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
